// Logisim project MicroProgrammed Computer .circ as structural Verilog
module main (
  input  in_1
);

  wire AR_OR_DR, CLR_AC, CLR_AR, CLR_CAR, CLR_DR, CLR_PC, I, INC_AC, INC_AR, INC_CAR, INC_DR, INC_PC, LD_AC,
       LD_AR, LD_CAR, LD_DR, LD_PC, LD_SBR, or_1_out, S, T, Z;
  wire [1:0] Branch_Logic_s0, PC_0__M_1__AC_2;
  wire [2:0] F1, F2, F3, S1_S0_CIN__ALU;
  wire [6:0] adder_1_out, CAR_output, Mapping_Logic_out_2, multiplexer_1_out, rom_1_data, SBR_output;
  wire [10:0] AR_output, DR_IR_output, multiplexer_3_out, PC_output;
  wire [10:7] rom_1_data_2;
  wire [14:0] AC_output;
  wire [15:0] ALU_out, multiplexer_4_out, ram_1_data;

  Branch_Logic Branch_Logic (
    .BR1(rom_1_data_2[10]), .BR0(rom_1_data_2[9]), .CD(T), .S0(Branch_Logic_s0[0]), .S1(Branch_Logic_s0[1]),
    .LDSBR(LD_SBR));
  Mapping Mapping_Logic (.in_1({4{I}}), .out_2(Mapping_Logic_out_2));
  Multiplexer #(.select(2), .width(7)) multiplexer_1 (
    .in0(adder_1_out), .in1(SBR_output), .in2(rom_1_data), .in3(Mapping_Logic_out_2),
    .out(multiplexer_1_out), .sel(Branch_Logic_s0));  // open: en
  Register_7bit CAR (
    .LD(LD_CAR), .INC(INC_CAR), .CLR(CLR_CAR), .\input (multiplexer_1_out), .\output (CAR_output));  // open: Clk
  ROM #(.addrWidth(7), .dataWidth(20)) rom_1 (
    .addr(CAR_output), .data({F1, F2, F3, rom_1_data_2, rom_1_data}));  // open: sel
  Adder #(.width(7)) adder_1 (.b(CAR_output), .out(adder_1_out), .cin(in_1));  // open: a, cout
  Multiplexer #(.select(2)) multiplexer_2 (
    .in0(1'b1), .in1(I), .in2(S), .in3(Z), .out(T), .sel(rom_1_data_2[8:7]));  // open: en
  Register_7bit SBR (
    .LD(LD_CAR), .INC(INC_CAR), .CLR(CLR_CAR), .\input (adder_1_out), .\output (SBR_output));  // open: Clk
  Multiplexer #(.width(11)) multiplexer_3 (
    .in0(PC_output), .in1(DR_IR_output), .out(multiplexer_3_out), .sel(AR_OR_DR));  // open: en
  Register_11bit AR (
    .\input (multiplexer_3_out), .\output (AR_output), .LD(LD_AR), .INC(INC_AR), .CLR(CLR_AR));  // open: Clk
  Register_11bit PC (.\input (AR_output), .\output (PC_output), .LD(LD_PC), .INC(INC_PC), .CLR(CLR_PC));  // open: Clk
  Multiplexer #(.select(2), .width(16)) multiplexer_4 (
    .in0({{5{1'b0}}, PC_output}), .in1(ram_1_data), .in2({S, AC_output}), .out(multiplexer_4_out),
    .sel(PC_0__M_1__AC_2));  // open: in3, en
  ALU ALU (
    .DR({{5{I}}, DR_IR_output}), .AC({S, AC_output}), .S1(S1_S0_CIN__ALU[0]), .S0(S1_S0_CIN__ALU[1]),
    .Cin(S1_S0_CIN__ALU[2]), .out(ALU_out));
  RAM #(.addrWidth(11), .dataWidth(16)) ram_1 (.addr(AR_output), .data(ram_1_data));  // open: sel, clk, ld, clr
  Register_16bit DR_IR (
    .\input (multiplexer_4_out), .\output ({{5{I}}, DR_IR_output}), .LD(LD_DR), .INC(INC_DR), .CLR(CLR_DR));  // open: Clk
  Register_16bit AC (
    .\input (ALU_out), .\output ({S, AC_output}), .LD(LD_AC), .INC(INC_AC), .CLR(CLR_AC));  // open: Clk
  or or_1 (or_1_out, AC_output[0], AC_output[1], AC_output[2], AC_output[3], AC_output[4], AC_output[5], AC_output[6], AC_output[7], AC_output[8], AC_output[9], AC_output[10], AC_output[11], AC_output[12], AC_output[13], AC_output[14], S);
  not not_1 (Z, or_1_out);
  // also tied to GND on the sheet: I

  // Other names for the same wires on the sheet: Opcode[3:0] = {4{I}}
endmodule

module Branch_Logic (
  input  BR0,
  input  BR1,
  input  CD,
  output S0,
  output S1,
  output LDSBR
);

  wire and_1_out, and_2_out, not_1_out, not_2_out;

  not not_1 (not_1_out, BR1);
  and and_1 (and_1_out, not_1_out, CD);
  and and_2 (and_2_out, BR1, BR0);
  and and_3 (LDSBR, BR0, CD, not_2_out);
  not not_2 (not_2_out, BR1);
  or or_1 (S0, and_1_out, and_2_out);

  assign S1 = BR1;
endmodule

module Register_7bit (
  input  [6:0] \input ,
  input  Clk,
  input  LD,
  input  INC,
  input  CLR,
  output [6:0] \output 
);

  wire decoder_1_out1, decoder_1_out2, decoder_1_out3;
  wire [1:0] priority_encoder_1_out;
  wire [6:0] adder_1_out;

  Priority_Encoder #(.select(2)) priority_encoder_1 (
    .in0(1'b0), .in1(LD), .in2(INC), .in3(CLR), .out(priority_encoder_1_out));  // open: gs, en_out, en_in
  Decoder #(.select(2)) decoder_1 (
    .out1(decoder_1_out1), .out2(decoder_1_out2), .out3(decoder_1_out3), .sel(priority_encoder_1_out));  // open: out0, en
  Adder #(.width(7)) adder_1 (.a(\input ), .b({7{1'b0}}), .out(adder_1_out), .cin(decoder_1_out2));  // open: cout
  Shift_Register #(.width(7), .length(1)) shift_register_1 (
    .in(adder_1_out), .clk(Clk), .out(\output ), .load(decoder_1_out1), .clr(decoder_1_out3));  // open: shift, d0, q0
endmodule

module branch_logic (
  input  BR1,
  input  BR0,
  input  CD,
  output S1,
  output S0,
  output LDSBR
);

  wire and_1_out, and_2_out, not_1_out, not_2_out;

  not not_1 (not_1_out, BR1);
  not not_2 (not_2_out, BR1);
  and and_1 (and_1_out, not_2_out, CD);
  and and_2 (and_2_out, BR1, BR0);
  and and_3 (LDSBR, BR0, CD, not_1_out);
  or or_1 (S0, and_1_out, and_2_out);

  assign S1 = BR1;
endmodule

module Mapping (
  input  [3:0] in_1,
  output [6:0] out_2
);


  assign out_2 = {1'b0, in_1, 2'b00};
endmodule

module Register_16bit (
  input  [15:0] \input ,
  input  Clk,
  input  LD,
  input  INC,
  input  CLR,
  output [15:0] \output 
);

  wire decoder_1_out1, decoder_1_out2, decoder_1_out3;
  wire [1:0] priority_encoder_1_out;
  wire [15:0] adder_1_out;

  Priority_Encoder #(.select(2)) priority_encoder_1 (
    .in0(1'b0), .in1(LD), .in2(INC), .in3(CLR), .out(priority_encoder_1_out));  // open: gs, en_out, en_in
  Decoder #(.select(2)) decoder_1 (
    .out1(decoder_1_out1), .out2(decoder_1_out2), .out3(decoder_1_out3), .sel(priority_encoder_1_out));  // open: out0, en
  Adder #(.width(16)) adder_1 (.a(\input ), .b({16{1'b0}}), .out(adder_1_out), .cin(decoder_1_out2));  // open: cout
  Shift_Register #(.width(16), .length(1)) shift_register_1 (
    .in(adder_1_out), .clk(Clk), .out(\output ), .load(decoder_1_out1), .clr(decoder_1_out3));  // open: shift, d0, q0
endmodule

module ALU (
  input  [15:0] DR,
  input  [15:0] AC,
  input  S1,
  input  S0,
  input  Cin,
  output [15:0] out
);
endmodule

module Register_11bit (
  input  [10:0] \input ,
  input  Clk,
  input  LD,
  input  INC,
  input  CLR,
  output [10:0] \output 
);

  wire decoder_1_out1, decoder_1_out2, decoder_1_out3;
  wire [1:0] priority_encoder_1_out;
  wire [10:0] adder_1_out;

  Priority_Encoder #(.select(2)) priority_encoder_1 (
    .in0(1'b0), .in1(LD), .in2(INC), .in3(CLR), .out(priority_encoder_1_out));  // open: gs, en_out, en_in
  Decoder #(.select(2)) decoder_1 (
    .out1(decoder_1_out1), .out2(decoder_1_out2), .out3(decoder_1_out3), .sel(priority_encoder_1_out));  // open: out0, en
  Adder #(.width(11)) adder_1 (.a(\input ), .b({11{1'b0}}), .out(adder_1_out), .cin(decoder_1_out2));  // open: cout
  Shift_Register #(.width(11), .length(1)) shift_register_1 (
    .in(adder_1_out), .clk(Clk), .out(\output ), .load(decoder_1_out1), .clr(decoder_1_out3));  // open: shift, d0, q0
endmodule
